# Fritzing sketch Estacion de radiacion (saved by Fritzing 0.9.3b)
breadboards: 1

parts:
  Componente1 = Arduino Uno (Rev3)
  PCB2 = RTC_DS1302_module
  microSD1 = MicroSD Card Module
  C1 = Electrolytic Capacitor [capacitance=10µF package="100 mil [THT, electrolytic]"]
  R1 = Resistor [tolerance=±5% resistance=10k package=THT]
  R2 = Resistor [tolerance=±5% resistance=10k package=THT]
  R3 = Resistor [tolerance=±5% resistance=220 package=THT]
  RHT1 = Humidity and Temperature Sensor RHT03
  R4 = Resistor [tolerance=±5% resistance=10k package=THT]
  LED1 = LED - 5mm [color="Red (633nm)" package="5 mm [THT]"]
  R5 = Resistor [tolerance=±5% resistance=220 package=THT]

nets:
  N1: Componente1.A0, R3.Pin_0
  N2: Componente1.A1, LED1.anode, R5.Pin_0
  N3: Componente1.D8, PCB2.RST
  N4: Componente1.D10_PWM/SS, microSD1.CS
  N5: Componente1.D11_PWM/MOSI, microSD1.MOSI
  N6: Componente1.D12/MISO, microSD1.MISO
  N7: Componente1.D13/SCK, microSD1.SCK
  N8: Componente1.D4, RHT1.Data-signal, R4.Pin_1
  N9: Componente1.D6_PWM, PCB2.CLK
  N10: Componente1.D7, PCB2.DAT
  VCC: Componente1.5V, PCB2.VCC, microSD1.VCC, R2.Pin_1, RHT1.Vcc, R4.Pin_0, LED1.cathode
  GND: Componente1.GND, PCB2.GND, microSD1.GND, C1.-, R1.Pin_0, RHT1.GND_2, R5.Pin_1
  N11: C1.+, R1.Pin_1, R2.Pin_0, R3.Pin_1

notes:
  SCT013

custom parts:
  RTC_DS1302_module: Arduino module DS1302 SPI Real Time Clock
